# Fritzing sketch wwvb (saved by Fritzing 0.9.2b)

parts:
  Part3 = Arduino Nano (Rev3.0)
  ANT3 = Antenna
  LED1 = Ruby the Red LED
  R = Resistor [tolerance=±5% resistance=110 package="2010 [SMD]"]
  C = Ceramic Capacitor [capacitance=1µF package="100 mil [THT, multilayer]"]
  R4 = Resistor [tolerance=±5% resistance=110 package=THT]
  Part4 = Arduino Nano (Rev3.0)
  U5 = attiny85 [package=dip]
  U6 = LM 358 Dual Op-Amp [package="DIP8 [THT]"]
  R2_1 = Resistor [tolerance=±5% resistance=10k package=THT]
  R1_1 = Resistor [tolerance=±5% resistance=1.5k package=THT]
  U7 = Voltage Regulator - 5V [package="DPak [SMD]"]
  Power_plug1 = Power plug
  U9 = LM 358 Dual Op-Amp [package="DIP8 [THT]"]
  ANT6 = Antenna
  R2_2 = Resistor [tolerance=±5% resistance=10k package=THT]
  R1_2 = Resistor [tolerance=±5% resistance=1.5k package=THT]
  J1 = PCD8544 LCD [form="♂ (male)" package=THT]
  GPS1 = Adafruit Ultimate GPS Breakout
  U10 = Chip antenna [package=antenna-chip4]
  LED2 = Ruby the Red LED

nets:
  N1: Part3.GND, LED1.anode, C.1
  N2: Part3.D9, ANT3.antenna_lead, R.Pin_0, R4.Pin_0
  N3: LED1.cathode, R.Pin_1, C.0, R4.Pin_1
  GND: Part4.GND, U9.connector3, J1.GND, GPS1.GND
  N4: Part4.D2, J1.DC
  N5: Part4.D3, J1.CE
  N6: Part4.D4, J1.RST
  N7: Part4.D6, GPS1.RX
  N8: Part4.D7, GPS1.TX
  N9: Part4.D8, R1_2.Pin_0
  N10: Part4.D9, R2_2.Pin_0
  N11: Part4.D11/MOSI, J1.DIN
  N12: Part4.5V, U9.connector7
  3V3: Part4.3V3, J1.VCC, GPS1.3.3V
  N13: Part4.D13/SCK, J1.CLK
  N14: U5.Pin_2, R1_1.Pin_0
  N15: U5.Pin_3, R2_1.Pin_0
  GND_2: U5.Pin_4, U6.connector3, U7.GND, Power_plug1.GND, LED2.cathode
  N16: U5.Pin_8, U6.connector7, U7.output_voltage
  N17: U6.connector0, U6.connector1, U10.SIGNAL
  N18: U6.connector2, R2_1.Pin_1, R1_1.Pin_1
  N19: U7.input_voltage, Power_plug1.VCC
  N20: U9.connector0, U9.connector1, ANT6.antenna_lead
  N21: U9.connector2, R2_2.Pin_1, R1_2.Pin_1

notes:
  Amplitude Modulation using internal PWM (debug circuit also shown)
  magenta : modulation signal
  blue : modulated output
  cyan : carrier signal
  Note : DEBUG circuit (LPF circuit) not required
  AM_gps_time_sync_nokia5110.ino
  ATtiny85_60kHz_and_1Hz.ino
  CLK
  Nokia 5110 header
  Real antenna setup
  output -> antenna -> limiting LED or resistor -> ground
  minimum.ino
  Amplitude Modulation using a summing op amp

custom parts:
  PCD8544 LCD: generic Nokia 5110 LCD
